# Fritzing sketch arduino-setup (saved by Fritzing 0.8.5b)
breadboards: 1

parts:
  Componente1 = Arduino Uno (Rev3)  # not connected
  Componente2 = Arduino Ethernet Shield (Rev3)
  R1 = Photocell (LDR) [package=THT]
  R2 = Resistor [tolerance=±5% resistance=220 package=THT]

nets:
  N1: Componente2.A0, R1.pin_0, R2.Pin_0
  N2: Componente2.5V, R1.pin_1
  N3: Componente2.GND, R2.Pin_1
